# Fritzing sketch vOICeOnPi-Rev33 (saved by Fritzing 0.9.2b)
circuit board: 5.63626cm x 8.53488cm
breadboards: 1

parts:
  100uF = Capacitor Polarized [package=cpol-radial-100uf-25v]
  100Ohm = Resistor [tolerance=±5% resistance=100 package=THT]
  1N4001 = Rectifier Diode [part_number=1N4001 package="300 mil [THT]"]
  J1 = female pin header, 20 pins [form="♀ (female)"]
  J2 = female pin header, 20 pins [form="♀ (female)"]
  Vibe = Vibration Motor
  BC517 = NPN-Transistor [part_number=BC517 package="TO92 [THT]"]
  1k_Ohm = Resistor [tolerance=±5% resistance=1k package=THT]
  POWERBOOST_1000C = female pin header, 8 pins [form="♀ (female)"]
  J3 = female pin header, 3 pins [form="♀ (female)"]
  SONAR = female pin header, 7 pins [form="♀ (female)"]
  J4 = female pin header, 1 pin [form="♀ (female)"]
  J5 = female pin header, 1 pin [form="♀ (female)"]
  Rotary_SW = female pin header, 3 pins [form="♀ (female)"]
  BC516 = PNP-Transistor [part_number=BC516 package="TO92 [THT]"]
  1meg_OHM = Resistor [tolerance=±5% resistance=1M package=THT]
  220uF = Electrolytic Capacitor [capacitance=0.22mF package="100 mil [THT, electrolytic]"]
  10k_Ohm = Resistor [tolerance=±5% resistance=10k package=THT]
  future_SW = female pin header, 3 pins [form="♀ (female)"]
  on/on_Power_Sw = female pin header, 3 pins [form="♀ (female)"]
  330k_Ohm = Resistor [tolerance=±5% resistance=220 package=THT]
  100k_Ohm = Resistor [tolerance=±5% resistance=220 package=THT]

nets:
  N1: 100uF.+, 100Ohm.Pin_0, SONAR.pin6
  N2: 100uF.-, J2.pin5, BC517.E, POWERBOOST_1000C.pin2, POWERBOOST_1000C.pin4, SONAR.pin7, J5.pin1, Rotary_SW.pin2, BC516.E, 1meg_OHM.Pin_0, 220uF.-, 330k_Ohm.Pin_0
  N3: 100Ohm.Pin_1, J2.pin1
  N4: 1N4001.cathode, J1.pin1, Vibe.POS, POWERBOOST_1000C.pin1
  N5: 1N4001.anode, Vibe.NEG, BC517.C
  N6: J1.pin5, SONAR.pin5
  N7: J1.pin8, Rotary_SW.pin3
  N8: J1.pin9, Rotary_SW.pin1
  N9: J1.pin11, J4.pin1
  N10: J1.pin19, 1k_Ohm.Pin_1
  N11: J2.pin7, POWERBOOST_1000C.pin3
  N12: J2.pin10, 330k_Ohm.Pin_1, 100k_Ohm.Pin_1
  N13: J2.pin11, 10k_Ohm.Pin_1
  N14: BC517.B, 1k_Ohm.Pin_0
  N15: POWERBOOST_1000C.pin5, BC516.C
  N16: POWERBOOST_1000C.pin6, J3.pin1, future_SW.pin1, on/on_Power_Sw.pin1
  N17: POWERBOOST_1000C.pin8, 100k_Ohm.Pin_0
  N18: J3.pin2, BC516.B, 1meg_OHM.Pin_1, 220uF.+, on/on_Power_Sw.pin2
  N19: J3.pin3, 10k_Ohm.Pin_0, future_SW.pin3, on/on_Power_Sw.pin3

custom parts:
  Vibration Motor: An eccentric vibration motor!
